// Logisim project exercice_cours_14.circ as structural Verilog: 1 circuit, main circuit main
module main (
  input  in_1,
  input  in_2,
  input  in_3,
  output out_4,
  output out_5
);

  wire and_1_out, not_1_out;

  and and_1 (and_1_out, in_1, in_2);
  not not_1 (not_1_out, in_2);
  or or_1 (out_4, and_1_out, in_3);
  or or_2 (out_5, not_1_out, in_3);
endmodule
