// Logisim project Circuit-2.circ as structural Verilog: 1 circuit, main circuit main
module main (
  input  bit_4,
  input  bit_3,
  input  bit_2,
  input  bit_1
);

  wire and_1_out, and_2_out, and_3_out, and_4_out, not_1_out, not_2_out, not_3_out, or_1_out, or_2_out,
       or_3_out;

  not not_1 (not_1_out, bit_4);
  not not_2 (not_2_out, bit_3);
  not not_3 (not_3_out, bit_2);
  and and_1 (and_1_out, not_2_out, bit_2);
  or or_1 (or_1_out, bit_1, not_1_out);
  and and_2 (and_2_out, bit_1, bit_3);
  or or_2 (or_2_out, not_3_out, not_1_out);
  and and_3 (and_3_out, and_1_out, or_1_out);
  and and_4 (and_4_out, and_2_out, or_2_out);
  or or_3 (or_3_out, and_3_out, and_4_out);
  LED led_1 (.in(or_3_out));

  // Notes on the sheet:
  //   bit de poid faible
endmodule
